// Logisim project 8-bit_load-store_processor.circ as structural Verilog: 2 circuits, main circuit main
module main (
  output CC,
  output [15:0] valM,
  output [15:0] valE,
  output [15:0] valA,
  output [15:0] valB,
  output [15:0] valC,
  output [3:0] icode,
  output [3:0] ifun,
  output [3:0] rA,
  output [3:0] rB,
  output [15:0] valP,
  output [15:0] PC,
  output [15:0] newPC
);

  wire alu_1_cc, clock_1_clock, fetch_1_halt, fetch_1_need_regids, fetch_1_need_valc, mem_read_1_op,
       mem_write_1_op, set_cc_1_out_2;
  wire [3:0] alu_fun_1_out_4;
  wire [15:0] alu_a_1_a___c, alu_b_1_b___0, mem_addr_1_op, mem_data_1_op;

  Counter #(.width(4), .max('hb), .ongoal("load")) counter_1 (.clk(clock_1_clock));  // open: load, D, count, Q, carry, clr
  clock clock_1 (.halt(fetch_1_halt), .clock(clock_1_clock));
  CC cc_1 (.clock(clock_1_clock), .CC(CC), .Set_CC(set_cc_1_out_2), .ALU_CC(alu_1_cc));
  Set_CC set_cc_1 (.out_2(set_cc_1_out_2), .icode(icode));
  ALU alu_1 (
    .CC(alu_1_cc), .clock(clock_1_clock), .valE(valE), .ALU_A(alu_a_1_a___c), .ALU_B(alu_b_1_b___0),
    .ALU_Fun(alu_fun_1_out_4));
  ALU_A alu_a_1 (.icode(icode), .cycle(clock_1_clock), .A___C(alu_a_1_a___c), .valA(valA), .valC(valC));
  FETCH fetch_1 (
    .clock(clock_1_clock), .halt(fetch_1_halt), .Need_valC(fetch_1_need_valc),
    .Need_Regids(fetch_1_need_regids), .icode(icode), .ifun(ifun), .rA(rA), .rB(rB), .valC(valC), .PC(PC));
  PC pc_1 (.clock(clock_1_clock), .current_PC(PC), .newPC(newPC));
  ALU_Fun alu_fun_1 (.out_4(alu_fun_1_out_4), .cycle(clock_1_clock), .icode(icode), .ifun(ifun));
  ALU_B alu_b_1 (.icode(icode), .cycle(clock_1_clock), .B___0(alu_b_1_b___0), .valB(valB));
  NEW_PC new_pc_1 (.clock(clock_1_clock), .newPC(newPC), .icode(icode), .ifun(ifun), .CC(CC), .valC(valC), .valP(valP));
  PC_INCREMENT pc_increment_1 (.Need_valC(fetch_1_need_valc), .Need_Regids(fetch_1_need_regids), .valP(valP), .PC(PC));
  Mem_Read mem_read_1 (.ICODE(icode), .op(mem_read_1_op));
  Mem_Write mem_write_1 (.ICODE(icode), .op(mem_write_1_op));
  Mem_Addr mem_addr_1 (.OP(mem_addr_1_op), .ICODE(icode), .VAL_E(valE));
  DMem dmem_1 (
    .clock(clock_1_clock), .Read(mem_read_1_op), .Address(mem_addr_1_op), .Write(mem_write_1_op),
    .Data(mem_data_1_op), .valM(valM));
  Mem_Data mem_data_1 (.OP(mem_data_1_op), .ICODE(icode), .VAL_A(valA));
  Register_File register_file_1 (
    .valA(valA), .valB(valB), .valM(valM), .valE(valE), .srcA(rA), .dstA(rA), .srcB(rB), .dstB(rB),
    .clock(clock_1_clock), .icode(icode));

  // Notes on the sheet:
  //   cycle counter
  //   clock
  //   Fetch
  //   PC
  //   NEW PC
  //   READ
  //   WRITE
  //   PC Increment
  //   Memory
  //   ADDR
  //   DATA
  //   Registers
endmodule

module clock (
  input  halt,
  output clock
);

  wire and_1_out, clock_1_out, comparator_1_eq;

  Clock clock_1 (.out(clock_1_out));
  Comparator #(.width(1), .mode("unsigned")) comparator_1 (.a(1'b0), .b(halt), .eq(comparator_1_eq));  // open: gt, lt
  assign clock = and_1_out ? clock_1_out : 1'bz;  // Controlled_Buffer controlled_buffer_1
  buf and_1 (and_1_out, comparator_1_eq);  // AND_Gate
endmodule
