// Logisim project decode_writeback.circ as structural Verilog: 6 circuits, main circuit main
module main (
  input  [15:0] Val_M,
  input  [15:0] Val_E,
  input  [3:0] icode,
  input  [3:0] rA,
  input  [3:0] rB,
  output [15:0] Val_A,
  output [15:0] Val_B
);

  wire clock_1_out;

  Clock clock_1 (.out(clock_1_out));
  // Register_File register_file_1: pin names not known; wires that end beside it: clock_1_out, icode, rA
endmodule

module Register_File (
  input  [15:0] valM,
  input  [15:0] valE,
  input  [3:0] dstA,
  input  [3:0] srcA,
  input  [3:0] srcB,
  input  [3:0] dstB,
  input  clock,
  input  [3:0] icode,
  output [15:0] valA,
  output [15:0] valB
);

  wire and_1_out, comparator_1_eq, comparator_2_gt, decoder_1_out1, decoder_1_out2, decoder_1_out3,
       decoder_1_out4, decoder_1_out5, decoder_2_out0, decoder_2_out1, decoder_2_out2, decoder_2_out3,
       decoder_2_out4, decoder_2_out5, decoder_2_out6, decoder_2_out7, decoder_3_out0, decoder_3_out1,
       decoder_3_out2, decoder_3_out3, decoder_3_out4, decoder_3_out5, decoder_3_out6, decoder_3_out7,
       decoder_4_out0, decoder_4_out1, decoder_4_out2, decoder_4_out3, decoder_4_out4, decoder_4_out5,
       decoder_4_out6, decoder_4_out7, decoder_5_out0, decoder_5_out1, decoder_5_out2, decoder_5_out3,
       decoder_5_out4, decoder_5_out5, decoder_5_out6, decoder_5_out7, dstA_out, dstB_out, not_1_out,
       not_2_out, or_1_out, or_2_out, or_3_out, or_4_out, or_5_out, or_6_out, or_7_out, or_8_out, srcA_out,
       srcB_out, valE_out;
  wire [3:0] controlled_buffer_1_out, controlled_buffer_3_out, counter_1_q;
  wire [15:0] ax_0_q, bp_5_q, bx_3_q, controlled_buffer_5_out, controlled_buffer_7_out,
       controlled_buffer_9_out, controlled_buffer_11_out, controlled_buffer_13_out, controlled_buffer_15_out,
       controlled_buffer_17_out, controlled_buffer_19_out, controlled_buffer_21_out,
       controlled_buffer_22_out, controlled_buffer_23_out, controlled_buffer_24_out,
       controlled_buffer_25_out, controlled_buffer_26_out, controlled_buffer_27_out,
       controlled_buffer_28_out, controlled_buffer_29_out, controlled_buffer_37_out, cx_1_q, di_7_q, dx_2_q,
       si_6_q, sp_4_q;

  not not_1 (not_1_out, dstA_out);
  not not_2 (not_2_out, dstB_out);
  assign controlled_buffer_1_out = not_2_out ? 4'b1111 : 4'bz;  // Controlled_Buffer controlled_buffer_1
  assign controlled_buffer_1_out = dstB_out ? dstB : 4'bz;  // Controlled_Buffer controlled_buffer_2
  Decoder #(.select(4)) decoder_1 (
    .out1(decoder_1_out1), .out2(decoder_1_out2), .out3(decoder_1_out3), .out4(decoder_1_out4),
    .out5(decoder_1_out5), .sel(icode));  // open: out0, out6, out7, out8, out9, out10, out11, out12, out13, out14, out15, en
  assign controlled_buffer_3_out = dstA_out ? dstA : 4'bz;  // Controlled_Buffer controlled_buffer_3
  assign controlled_buffer_3_out = not_1_out ? 4'b1111 : 4'bz;  // Controlled_Buffer controlled_buffer_4
  Decoder #(.select(4)) decoder_2 (
    .out0(decoder_2_out0), .out1(decoder_2_out1), .out2(decoder_2_out2), .out3(decoder_2_out3),
    .out4(decoder_2_out4), .out5(decoder_2_out5), .out6(decoder_2_out6), .out7(decoder_2_out7),
    .sel(controlled_buffer_3_out));  // open: out8, out9, out10, out11, out12, out13, out14, out15, en
  Decoder #(.select(4)) decoder_3 (
    .out0(decoder_3_out0), .out1(decoder_3_out1), .out2(decoder_3_out2), .out3(decoder_3_out3),
    .out4(decoder_3_out4), .out5(decoder_3_out5), .out6(decoder_3_out6), .out7(decoder_3_out7),
    .sel(controlled_buffer_1_out));  // open: out8, out9, out10, out11, out12, out13, out14, out15, en
  or u_valE (valE_out, decoder_1_out1, decoder_1_out2, decoder_1_out5);
  or u_srcA (srcA_out, decoder_1_out1, decoder_1_out4, decoder_1_out5);
  or u_srcB (srcB_out, decoder_1_out1, decoder_1_out5, decoder_1_out3, decoder_1_out4);
  or u_dstA (dstA_out, decoder_1_out2, decoder_1_out3, decoder_1_out5);
  buf u_dstB (dstB_out, decoder_1_out1);  // OR_Gate
  assign controlled_buffer_5_out = decoder_1_out3 ? valM : 16'bz;  // Controlled_Buffer controlled_buffer_5
  assign controlled_buffer_5_out = valE_out ? valE : 16'bz;  // Controlled_Buffer controlled_buffer_6
  assign controlled_buffer_7_out = decoder_1_out3 ? valM : 16'bz;  // Controlled_Buffer controlled_buffer_7
  assign controlled_buffer_7_out = valE_out ? valE : 16'bz;  // Controlled_Buffer controlled_buffer_8
  assign controlled_buffer_9_out = decoder_1_out3 ? valM : 16'bz;  // Controlled_Buffer controlled_buffer_9
  assign controlled_buffer_9_out = valE_out ? valE : 16'bz;  // Controlled_Buffer controlled_buffer_10
  assign controlled_buffer_11_out = decoder_1_out3 ? valM : 16'bz;  // Controlled_Buffer controlled_buffer_11
  assign controlled_buffer_11_out = valE_out ? valE : 16'bz;  // Controlled_Buffer controlled_buffer_12
  assign controlled_buffer_13_out = decoder_1_out3 ? valM : 16'bz;  // Controlled_Buffer controlled_buffer_13
  assign controlled_buffer_13_out = valE_out ? valE : 16'bz;  // Controlled_Buffer controlled_buffer_14
  assign controlled_buffer_15_out = decoder_1_out3 ? valM : 16'bz;  // Controlled_Buffer controlled_buffer_15
  assign controlled_buffer_15_out = valE_out ? valE : 16'bz;  // Controlled_Buffer controlled_buffer_16
  assign controlled_buffer_17_out = decoder_1_out3 ? valM : 16'bz;  // Controlled_Buffer controlled_buffer_17
  assign controlled_buffer_17_out = valE_out ? valE : 16'bz;  // Controlled_Buffer controlled_buffer_18
  assign controlled_buffer_19_out = decoder_1_out3 ? valM : 16'bz;  // Controlled_Buffer controlled_buffer_19
  assign controlled_buffer_19_out = valE_out ? valE : 16'bz;  // Controlled_Buffer controlled_buffer_20
  or or_1 (or_1_out, decoder_2_out0, decoder_3_out0);
  or or_2 (or_2_out, decoder_2_out1, decoder_3_out1);
  or or_3 (or_3_out, decoder_2_out2, decoder_3_out2);
  or or_4 (or_4_out, decoder_2_out3, decoder_3_out3);
  or or_5 (or_5_out, decoder_2_out4, decoder_3_out4);
  assign controlled_buffer_21_out = or_1_out ? controlled_buffer_5_out : 16'bz;  // Controlled_Buffer controlled_buffer_21
  assign controlled_buffer_22_out = or_2_out ? controlled_buffer_7_out : 16'bz;  // Controlled_Buffer controlled_buffer_22
  assign controlled_buffer_23_out = or_3_out ? controlled_buffer_9_out : 16'bz;  // Controlled_Buffer controlled_buffer_23
  assign controlled_buffer_24_out = or_4_out ? controlled_buffer_11_out : 16'bz;  // Controlled_Buffer controlled_buffer_24
  assign controlled_buffer_25_out = or_5_out ? controlled_buffer_13_out : 16'bz;  // Controlled_Buffer controlled_buffer_25
  assign controlled_buffer_26_out = or_6_out ? controlled_buffer_15_out : 16'bz;  // Controlled_Buffer controlled_buffer_26
  assign controlled_buffer_27_out = or_7_out ? controlled_buffer_17_out : 16'bz;  // Controlled_Buffer controlled_buffer_27
  or or_6 (or_6_out, decoder_2_out5, decoder_3_out5);
  or or_7 (or_7_out, decoder_2_out6, decoder_3_out6);
  or or_8 (or_8_out, decoder_2_out7, decoder_3_out7);
  Register #(.width(16)) ax_0 (.D(controlled_buffer_21_out), .en(and_1_out), .Q(ax_0_q), .clk(and_1_out));  // open: clr
  Register #(.width(16)) cx_1 (.D(controlled_buffer_22_out), .en(and_1_out), .Q(cx_1_q), .clk(and_1_out));  // open: clr
  Register #(.width(16)) dx_2 (.D(controlled_buffer_23_out), .en(and_1_out), .Q(dx_2_q), .clk(and_1_out));  // open: clr
  Register #(.width(16)) bx_3 (.D(controlled_buffer_24_out), .en(and_1_out), .Q(bx_3_q), .clk(and_1_out));  // open: clr
  Register #(.width(16)) sp_4 (.D(controlled_buffer_25_out), .en(and_1_out), .Q(sp_4_q), .clk(and_1_out));  // open: clr
  Register #(.width(16)) bp_5 (.D(controlled_buffer_26_out), .en(and_1_out), .Q(bp_5_q), .clk(and_1_out));  // open: clr
  Register #(.width(16)) si_6 (.D(controlled_buffer_27_out), .en(and_1_out), .Q(si_6_q), .clk(and_1_out));  // open: clr
  assign controlled_buffer_28_out = or_8_out ? controlled_buffer_19_out : 16'bz;  // Controlled_Buffer controlled_buffer_28
  Register #(.width(16)) di_7 (.D(controlled_buffer_28_out), .en(and_1_out), .Q(di_7_q), .clk(and_1_out));  // open: clr
  Counter #(.width(4), .max('hb)) counter_1 (.Q(counter_1_q), .clk(clock));  // open: load, D, count, carry, clr
  Register #(.width(16)) register_1 (
    .D(controlled_buffer_29_out), .en(srcA_out), .Q(valA), .clk(comparator_1_eq));  // open: clr
  assign controlled_buffer_29_out = decoder_4_out0 ? ax_0_q : 16'bz;  // Controlled_Buffer controlled_buffer_29
  assign controlled_buffer_29_out = decoder_4_out1 ? cx_1_q : 16'bz;  // Controlled_Buffer controlled_buffer_30
  assign controlled_buffer_29_out = decoder_4_out2 ? dx_2_q : 16'bz;  // Controlled_Buffer controlled_buffer_31
  assign controlled_buffer_29_out = decoder_4_out3 ? bx_3_q : 16'bz;  // Controlled_Buffer controlled_buffer_32
  assign controlled_buffer_29_out = decoder_4_out4 ? sp_4_q : 16'bz;  // Controlled_Buffer controlled_buffer_33
  assign controlled_buffer_29_out = decoder_4_out5 ? bp_5_q : 16'bz;  // Controlled_Buffer controlled_buffer_34
  assign controlled_buffer_29_out = decoder_4_out6 ? si_6_q : 16'bz;  // Controlled_Buffer controlled_buffer_35
  assign controlled_buffer_29_out = decoder_4_out7 ? di_7_q : 16'bz;  // Controlled_Buffer controlled_buffer_36
  Comparator #(.width(4), .mode("unsigned")) comparator_1 (
    .a(counter_1_q), .b(4'b0011), .eq(comparator_1_eq));  // open: gt, lt
  and and_1 (and_1_out, clock, comparator_2_gt);
  Comparator #(.width(4), .mode("unsigned")) comparator_2 (
    .a(counter_1_q), .b(4'b1001), .gt(comparator_2_gt));  // open: eq, lt
  assign controlled_buffer_37_out = decoder_5_out0 ? ax_0_q : 16'bz;  // Controlled_Buffer controlled_buffer_37
  assign controlled_buffer_37_out = decoder_5_out1 ? cx_1_q : 16'bz;  // Controlled_Buffer controlled_buffer_38
  assign controlled_buffer_37_out = decoder_5_out2 ? dx_2_q : 16'bz;  // Controlled_Buffer controlled_buffer_39
  assign controlled_buffer_37_out = decoder_5_out3 ? bx_3_q : 16'bz;  // Controlled_Buffer controlled_buffer_40
  Decoder #(.select(4)) decoder_4 (
    .out0(decoder_4_out0), .out1(decoder_4_out1), .out2(decoder_4_out2), .out3(decoder_4_out3),
    .out4(decoder_4_out4), .out5(decoder_4_out5), .out6(decoder_4_out6), .out7(decoder_4_out7), .sel(srcA));  // open: out8, out9, out10, out11, out12, out13, out14, out15, en
  assign controlled_buffer_37_out = decoder_5_out4 ? sp_4_q : 16'bz;  // Controlled_Buffer controlled_buffer_41
  assign controlled_buffer_37_out = decoder_5_out5 ? bp_5_q : 16'bz;  // Controlled_Buffer controlled_buffer_42
  assign controlled_buffer_37_out = decoder_5_out6 ? si_6_q : 16'bz;  // Controlled_Buffer controlled_buffer_43
  assign controlled_buffer_37_out = decoder_5_out7 ? di_7_q : 16'bz;  // Controlled_Buffer controlled_buffer_44
  Register #(.width(16)) register_2 (
    .D(controlled_buffer_37_out), .en(srcB_out), .Q(valB), .clk(comparator_1_eq));  // open: clr
  Decoder #(.select(4)) decoder_5 (
    .out0(decoder_5_out0), .out1(decoder_5_out1), .out2(decoder_5_out2), .out3(decoder_5_out3),
    .out4(decoder_5_out4), .out5(decoder_5_out5), .out6(decoder_5_out6), .out7(decoder_5_out7), .sel(srcB));  // open: out8, out9, out10, out11, out12, out13, out14, out15, en

  // Notes on the sheet:
  //   Val M
  //   Val E
  //   Val A
  //   Val B
endmodule

module dstE (
  input  [3:0] icode,
  input  [3:0] rB,
  input  clock,
  output [3:0] out
);

  wire decoder_1_out1, or_1_out;

  Decoder #(.select(4)) decoder_1 (
    .out1(decoder_1_out1), .sel(icode));  // open: out0, out2, out3, out4, out5, out6, out7, out8, out9, out10, out11, out12, out13, out14, out15, en
  buf or_1 (or_1_out, decoder_1_out1);  // OR_Gate
  Register #(.width(4)) register_1 (.D(rB), .en(or_1_out), .Q(out), .clk(clock));  // open: clr
endmodule

module dstM (
  input  [3:0] icode,
  input  [3:0] rA,
  input  clock,
  output [3:0] out
);

  wire decoder_1_out2, decoder_1_out3, or_1_out;

  Decoder #(.select(4)) decoder_1 (
    .out2(decoder_1_out2), .out3(decoder_1_out3), .sel(icode));  // open: out0, out1, out4, out5, out6, out7, out8, out9, out10, out11, out12, out13, out14, out15, en
  or or_1 (or_1_out, decoder_1_out2, decoder_1_out3);
  Register #(.width(4)) register_1 (.D(rA), .en(or_1_out), .Q(out), .clk(clock));  // open: clr
endmodule

module srcA (
  input  [3:0] icode,
  input  [3:0] rA,
  input  clock,
  output [3:0] out
);

  wire decoder_1_out1, decoder_1_out3, decoder_1_out4, decoder_1_out5, or_1_out;

  Decoder #(.select(4)) decoder_1 (
    .out1(decoder_1_out1), .out3(decoder_1_out3), .out4(decoder_1_out4), .out5(decoder_1_out5), .sel(icode));  // open: out0, out2, out6, out7, out8, out9, out10, out11, out12, out13, out14, out15, en
  or or_1 (or_1_out, decoder_1_out1, decoder_1_out3, decoder_1_out4, decoder_1_out5);
  Register #(.width(4)) register_1 (.D(rA), .en(or_1_out), .Q(out), .clk(clock));  // open: clr
endmodule

module srcB (
  input  [3:0] icode,
  input  [3:0] rB,
  input  clock,
  output [3:0] out
);

  wire decoder_1_out3, decoder_1_out4, decoder_1_out5, or_1_out;

  Decoder #(.select(4)) decoder_1 (
    .out3(decoder_1_out3), .out4(decoder_1_out4), .out5(decoder_1_out5), .sel(icode));  // open: out0, out1, out2, out6, out7, out8, out9, out10, out11, out12, out13, out14, out15, en
  or or_1 (or_1_out, decoder_1_out3, decoder_1_out4, decoder_1_out5);
  Register #(.width(4)) register_1 (.D(rB), .en(or_1_out), .Q(out), .clk(clock));  // open: clr
endmodule
