// Logisim project execute.circ as structural Verilog: 7 circuits, main circuit main
module main (
  input  clk,
  input  [3:0] icode,
  input  [3:0] ifun,
  input  [15:0] val_A,
  input  [15:0] val_C,
  input  [15:0] val_B,
  output CC,
  output [15:0] val_E
);

  wire alu_1_cc, set_cc_1_out_2;
  wire [3:0] alu_fun_1_out_4;
  wire [15:0] alu_a_1_a___c, alu_b_1_b___0;

  CC cc_1 (.clock(clk), .CC(CC), .Set_CC(set_cc_1_out_2), .ALU_CC(alu_1_cc));
  Set_CC set_cc_1 (.out_2(set_cc_1_out_2), .icode(icode));
  ALU_A alu_a_1 (.icode(icode), .cycle(clk), .A___C(alu_a_1_a___c), .valA(val_A), .valC(val_C));
  ALU alu_1 (
    .CC(alu_1_cc), .clock(clk), .valE(val_E), .ALU_A(alu_a_1_a___c), .ALU_B(alu_b_1_b___0),
    .ALU_Fun(alu_fun_1_out_4));
  ALU_Fun alu_fun_1 (.out_4(alu_fun_1_out_4), .cycle(clk), .icode(icode), .ifun(ifun));
  ALU_B alu_b_1 (.icode(icode), .cycle(clk), .B___0(alu_b_1_b___0), .valB(val_B));
endmodule

module ALU (
  input  clock,
  input  [3:0] ALU_Fun,
  input  [15:0] ALU_A,
  input  [15:0] ALU_B,
  output CC,
  output [15:0] valE
);

  wire and_1_out, buffer_1_out, buffer_2_out, comparator_1_eq, comparator_1_gt, comparator_1_lt,
       comparator_2_gt, decoder_1_out0, decoder_1_out1, or_1_out;
  wire [3:0] counter_1_q;
  wire [15:0] adder_1_out, controlled_buffer_1_out, multiplier_1_out;

  Counter #(.width(4), .max('hb)) counter_1 (.Q(counter_1_q), .clk(clock));  // open: load, D, count, carry, clr
  Comparator #(.width(16)) comparator_1 (
    .a({16{1'b0}}), .b(controlled_buffer_1_out), .gt(comparator_1_gt), .eq(comparator_1_eq),
    .lt(comparator_1_lt));
  Comparator #(.width(4), .mode("unsigned")) comparator_2 (
    .a(counter_1_q), .b(4'b0101), .gt(comparator_2_gt));  // open: eq, lt
  Register #(.width(1), .trigger("high")) register_1 (
    .D(comparator_1_eq), .Q(CC), .clk(and_1_out), .clr(or_1_out));  // open: en
  or or_1 (or_1_out, comparator_1_lt, comparator_1_gt);
  and and_1 (and_1_out, comparator_2_gt, clock);
  Multiplier #(.width(16)) multiplier_1 (.a(ALU_A), .b(ALU_B), .out(multiplier_1_out));  // open: cin, cout
  assign controlled_buffer_1_out = buffer_2_out ? multiplier_1_out : 16'bz;  // Controlled_Buffer controlled_buffer_1
  Register #(.width(16)) register_2 (.D(controlled_buffer_1_out), .Q(valE), .clk(and_1_out));  // open: en, clr
  assign controlled_buffer_1_out = buffer_1_out ? adder_1_out : 16'bz;  // Controlled_Buffer controlled_buffer_2
  Adder #(.width(16)) adder_1 (.a(ALU_A), .b(ALU_B), .out(adder_1_out));  // open: cin, cout
  buf buffer_1 (buffer_1_out, decoder_1_out0);
  buf buffer_2 (buffer_2_out, decoder_1_out1);
  Decoder #(.select(4)) decoder_1 (
    .out0(decoder_1_out0), .out1(decoder_1_out1), .sel(ALU_Fun));  // open: out2, out3, out4, out5, out6, out7, out8, out9, out10, out11, out12, out13, out14, out15, en
endmodule

module ALU_A (
  input  [3:0] icode,
  input  [15:0] valA,
  input  [15:0] valC,
  input  cycle,
  output [15:0] A___C
);

  wire and_1_out, buffer_1_out, buffer_2_out, buffer_3_out, buffer_4_out, buffer_5_out, comparator_1_gt,
       decoder_1_out1, decoder_1_out2, decoder_1_out3, decoder_1_out4, decoder_1_out5, or_1_out, or_2_out;
  wire [3:0] counter_1_q;
  wire [15:0] controlled_buffer_1_out;

  Decoder #(.select(4)) decoder_1 (
    .out1(decoder_1_out1), .out2(decoder_1_out2), .out3(decoder_1_out3), .out4(decoder_1_out4),
    .out5(decoder_1_out5), .sel(icode));  // open: out0, out6, out7, out8, out9, out10, out11, out12, out13, out14, out15, en
  buf buffer_1 (buffer_1_out, decoder_1_out2);
  buf buffer_2 (buffer_2_out, decoder_1_out3);
  buf buffer_3 (buffer_3_out, decoder_1_out4);
  Counter #(.width(4), .max('hb)) counter_1 (.Q(counter_1_q), .clk(cycle));  // open: load, D, count, carry, clr
  buf buffer_4 (buffer_4_out, decoder_1_out1);
  buf buffer_5 (buffer_5_out, decoder_1_out5);
  Comparator #(.width(4), .mode("unsigned")) comparator_1 (
    .a(counter_1_q), .b(4'b0100), .gt(comparator_1_gt));  // open: eq, lt
  or or_1 (or_1_out, buffer_1_out, buffer_2_out, buffer_3_out);
  or or_2 (or_2_out, buffer_4_out, buffer_5_out);
  and and_1 (and_1_out, comparator_1_gt, cycle);
  assign controlled_buffer_1_out = or_2_out ? valA : 16'bz;  // Controlled_Buffer controlled_buffer_1
  assign controlled_buffer_1_out = or_1_out ? valC : 16'bz;  // Controlled_Buffer controlled_buffer_2
  Register #(.width(16)) register_1 (.D(controlled_buffer_1_out), .Q(A___C), .clk(and_1_out));  // open: en, clr
endmodule

module ALU_B (
  input  [3:0] icode,
  input  [15:0] valB,
  input  cycle,
  output [15:0] B___0
);

  wire and_1_out, buffer_1_out, buffer_2_out, buffer_3_out, buffer_4_out, buffer_5_out, comparator_1_gt,
       decoder_1_out1, decoder_1_out2, decoder_1_out3, decoder_1_out4, decoder_1_out5, or_1_out, or_2_out;
  wire [3:0] counter_1_q;
  wire [15:0] controlled_buffer_1_out;

  Decoder #(.select(4)) decoder_1 (
    .out1(decoder_1_out1), .out2(decoder_1_out2), .out3(decoder_1_out3), .out4(decoder_1_out4),
    .out5(decoder_1_out5), .sel(icode));  // open: out0, out6, out7, out8, out9, out10, out11, out12, out13, out14, out15, en
  buf buffer_1 (buffer_1_out, decoder_1_out5);
  buf buffer_2 (buffer_2_out, decoder_1_out3);
  buf buffer_3 (buffer_3_out, decoder_1_out4);
  Counter #(.width(4), .max('hb)) counter_1 (.Q(counter_1_q), .clk(cycle));  // open: load, D, count, carry, clr
  buf buffer_4 (buffer_4_out, decoder_1_out1);
  buf buffer_5 (buffer_5_out, decoder_1_out2);
  or or_1 (or_1_out, buffer_1_out, buffer_2_out, buffer_3_out);
  or or_2 (or_2_out, buffer_4_out, buffer_5_out);
  Comparator #(.width(4), .mode("unsigned")) comparator_1 (
    .a(counter_1_q), .b(4'b0100), .gt(comparator_1_gt));  // open: eq, lt
  assign controlled_buffer_1_out = or_2_out ? {16{1'b0}} : 16'bz;  // Controlled_Buffer controlled_buffer_1
  and and_1 (and_1_out, comparator_1_gt, cycle);
  assign controlled_buffer_1_out = or_1_out ? valB : 16'bz;  // Controlled_Buffer controlled_buffer_2
  Register #(.width(16)) register_1 (.D(controlled_buffer_1_out), .Q(B___0), .clk(and_1_out));  // open: en, clr
endmodule

module ALU_Fun (
  input  [3:0] icode,
  input  [3:0] ifun,
  input  cycle,
  output [3:0] out_4
);

  wire and_1_out, buffer_1_out, buffer_2_out, comparator_1_gt, decoder_1_out5, decoder_1_out6, not_1_out,
       or_1_out;
  wire [3:0] controlled_buffer_1_out, counter_1_q;

  Decoder #(.select(4)) decoder_1 (
    .out5(decoder_1_out5), .out6(decoder_1_out6), .sel(icode));  // open: out0, out1, out2, out3, out4, out7, out8, out9, out10, out11, out12, out13, out14, out15, en
  buf buffer_1 (buffer_1_out, decoder_1_out5);
  Counter #(.width(4), .max('hb)) counter_1 (.Q(counter_1_q), .clk(cycle));  // open: load, D, count, carry, clr
  or or_1 (or_1_out, buffer_1_out, buffer_2_out);
  buf buffer_2 (buffer_2_out, decoder_1_out6);
  Comparator #(.width(4), .mode("unsigned")) comparator_1 (
    .a(counter_1_q), .b(4'b0100), .gt(comparator_1_gt));  // open: eq, lt
  assign controlled_buffer_1_out = or_1_out ? ifun : 4'bz;  // Controlled_Buffer controlled_buffer_1
  and and_1 (and_1_out, comparator_1_gt, cycle);
  Register #(.width(4)) register_1 (.D(controlled_buffer_1_out), .Q(out_4), .clk(and_1_out));  // open: en, clr
  not not_1 (not_1_out, or_1_out);
  assign controlled_buffer_1_out = not_1_out ? 4'b0000 : 4'bz;  // Controlled_Buffer controlled_buffer_2
endmodule

module Set_CC (
  input  [3:0] icode,
  output out_2
);

  wire decoder_1_out0, decoder_1_out1, decoder_1_out2, decoder_1_out3, decoder_1_out4, decoder_1_out5,
       decoder_1_out6, not_1_out, not_2_out, not_3_out, not_4_out, not_5_out, not_6_out;

  Decoder #(.select(4)) decoder_1 (
    .out0(decoder_1_out0), .out1(decoder_1_out1), .out2(decoder_1_out2), .out3(decoder_1_out3),
    .out4(decoder_1_out4), .out5(decoder_1_out5), .out6(decoder_1_out6), .sel(icode));  // open: out7, out8, out9, out10, out11, out12, out13, out14, out15, en
  not not_1 (not_1_out, decoder_1_out0);
  not not_2 (not_2_out, decoder_1_out1);
  not not_3 (not_3_out, decoder_1_out2);
  not not_4 (not_4_out, decoder_1_out3);
  not not_5 (not_5_out, decoder_1_out4);
  not not_6 (not_6_out, decoder_1_out6);
  and and_1 (out_2, not_1_out, not_2_out, not_3_out, not_4_out, not_5_out, decoder_1_out5, not_6_out);
endmodule

module CC (
  input  clock,
  input  ALU_CC,
  input  Set_CC,
  output CC
);

  wire and_1_out, comparator_1_gt;
  wire [3:0] counter_1_q;

  Counter #(.width(4), .max('hb)) counter_1 (.Q(counter_1_q), .clk(clock));  // open: load, D, count, carry, clr
  Comparator #(.width(4), .mode("unsigned")) comparator_1 (
    .a(counter_1_q), .b(4'b0110), .gt(comparator_1_gt));  // open: eq, lt
  and and_1 (and_1_out, comparator_1_gt, clock);
  Register #(.width(1)) register_1 (.D(ALU_CC), .en(Set_CC), .Q(CC), .clk(and_1_out));  // open: clr
endmodule
