// Logisim project fetch_pc.circ as structural Verilog: 5 circuits, main circuit main
module main (
  input  CC,
  output [3:0] icode,
  output [3:0] ifun,
  output [3:0] rA,
  output [3:0] rB,
  output [15:0] valC,
  output [15:0] pc,
  output [15:0] new_pc
);

  wire clock_1_out, comparator_1_eq, controlled_buffer_1_out, fetch_1_halt, fetch_1_need_regids,
       fetch_1_need_valc;
  wire [15:0] undriven;

  Counter #(.width(4), .max('ha), .ongoal("load")) counter_1 (.clk(clock_1_out));  // open: load, D, count, Q, carry, clr
  Clock clock_1 (.out(clock_1_out));
  Comparator #(.width(1), .mode("unsigned")) comparator_1 (
    .a(1'b0), .b(fetch_1_halt), .eq(comparator_1_eq));  // open: gt, lt
  assign controlled_buffer_1_out = comparator_1_eq ? clock_1_out : 1'bz;  // Controlled_Buffer controlled_buffer_1
  NEW_PC new_pc_1 (
    .clock(controlled_buffer_1_out), .newPC(new_pc), .icode(icode), .ifun(ifun), .CC(CC), .valC(valC),
    .valP(undriven));
  FETCH fetch_1 (
    .clock(controlled_buffer_1_out), .halt(fetch_1_halt), .Need_valC(fetch_1_need_valc),
    .Need_Regids(fetch_1_need_regids), .icode(icode), .ifun(ifun), .rA(rA), .rB(rB), .valC(valC), .PC(pc));
  PC pc_1 (.clock(controlled_buffer_1_out), .current_PC(pc), .newPC(new_pc));
  PC_INCREMENT pc_increment_1 (
    .Need_valC(fetch_1_need_valc), .Need_Regids(fetch_1_need_regids), .PC(pc));  // open: valP
endmodule

module PC_INCREMENT (
  input  Need_valC,
  input  Need_Regids,
  input  [15:0] PC,
  output [15:0] valP
);

  wire not_1_out;
  wire [15:0] adder_1_out, adder_2_out, bit_extender_1_out, controlled_buffer_1_out;

  not not_1 (not_1_out, Need_valC);
  assign controlled_buffer_1_out = Need_valC ? 16'h2 : 16'bz;  // Controlled_Buffer controlled_buffer_1
  assign controlled_buffer_1_out = not_1_out ? {16{1'b0}} : 16'bz;  // Controlled_Buffer controlled_buffer_2
  assign bit_extender_1_out = {{15{1'b0}}, Need_Regids};  // Bit_Extender bit_extender_1
  Adder #(.width(16)) adder_1 (
    .a(controlled_buffer_1_out), .b(bit_extender_1_out), .out(adder_1_out));  // open: cin, cout
  Adder #(.width(16)) adder_2 (.a(16'h1), .b(PC), .out(adder_2_out));  // open: cin, cout
  Adder #(.width(16)) adder_3 (.a(adder_1_out), .b(adder_2_out), .out(valP));  // open: cin, cout
endmodule

module FETCH (
  input  clock,
  input  [15:0] PC,
  output halt,
  output [15:0] valC,
  output Need_valC,
  output Need_Regids,
  output [3:0] icode,
  output [3:0] ifun,
  output [3:0] rA,
  output [3:0] rB
);

  wire and_1_out, and_2_out, and_3_out, and_4_out, and_5_out, and_6_out, and_7_out, and_8_out,
       comparator_1_gt, comparator_2_lt, comparator_3_eq, counter_1_carry, decoder_1_out0, decoder_1_out1,
       decoder_1_out2, decoder_1_out3, decoder_1_out4, decoder_2_out0, decoder_2_out1, decoder_2_out2,
       decoder_2_out3, decoder_2_out4, decoder_2_out5, decoder_2_out6, nor_1_out, not_1_out, not_2_out,
       or_1_out, or_2_out, or_3_out, or_4_out, or_5_out, rA_rB_2_out, rA_rB_3_out, rA_rB_out, valC_2_out,
       valC_3_out, valC_4_out, valC_5_out, valC_out, xor_1_out, xor_2_out;
  wire [3:0] counter_1_q, counter_2_q;
  wire [7:0] controlled_buffer_1_out, controlled_buffer_4_out, controlled_buffer_6_out,
       controlled_buffer_8_out, rom_1_data;
  wire [15:0] adder_1_out, adder_2_out, adder_3_out, controlled_buffer_2_out, register_3_q;

  ROM #(.addrWidth(16)) rom_1 (.addr(controlled_buffer_2_out), .data(rom_1_data), .sel(or_1_out));
  or or_1 (or_1_out, and_1_out, comparator_3_eq);
  assign controlled_buffer_1_out = or_4_out ? rom_1_data : 8'bz;  // Controlled_Buffer controlled_buffer_1
  assign controlled_buffer_2_out = or_3_out ? PC : 16'bz;  // Controlled_Buffer controlled_buffer_2
  Register register_1 (.D(controlled_buffer_1_out), .en(or_4_out), .Q({icode, ifun}), .clk(clock));  // open: clr
  assign controlled_buffer_2_out = decoder_1_out1 ? adder_1_out : 16'bz;  // Controlled_Buffer controlled_buffer_3
  Adder #(.width(16)) adder_1 (.a(16'h1), .b(PC), .out(adder_1_out));  // open: cin, cout
  assign controlled_buffer_4_out = rA_rB_out ? rom_1_data : 8'bz;  // Controlled_Buffer controlled_buffer_4
  Adder #(.width(16)) adder_2 (.a(16'h1), .b(adder_1_out), .out(adder_2_out));  // open: cin, cout
  Comparator #(.width(4), .mode("unsigned")) comparator_1 (
    .a(counter_1_q), .b(4'b0000), .gt(comparator_1_gt));  // open: eq, lt
  Register register_2 (.D(controlled_buffer_4_out), .en(rA_rB_out), .Q({rA, rB}), .clk(clock));  // open: clr
  Counter #(.width(4), .max('hb), .ongoal("load")) counter_1 (
    .Q(counter_1_q), .carry(counter_1_carry), .clk(clock));  // open: load, D, count, clr
  assign controlled_buffer_2_out = decoder_1_out2 ? adder_2_out : 16'bz;  // Controlled_Buffer controlled_buffer_5
  Register register_3 (.D(controlled_buffer_6_out), .en(valC_2_out), .Q(register_3_q[7:0]), .clk(clock));  // open: clr
  assign controlled_buffer_6_out = valC_2_out ? rom_1_data : 8'bz;  // Controlled_Buffer controlled_buffer_6
  assign controlled_buffer_2_out = decoder_1_out3 ? adder_3_out : 16'bz;  // Controlled_Buffer controlled_buffer_7
  Adder #(.width(16)) adder_3 (.a(16'h1), .b(adder_2_out), .out(adder_3_out));  // open: cin, cout
  Register #(.width(16)) register_4 (.D(register_3_q), .Q(valC), .clk(clock));  // open: en, clr
  Register register_5 (.D(controlled_buffer_8_out), .en(or_2_out), .Q(register_3_q[15:8]), .clk(clock));  // open: clr
  assign controlled_buffer_8_out = or_2_out ? rom_1_data : 8'bz;  // Controlled_Buffer controlled_buffer_8
  or or_2 (or_2_out, valC_4_out, valC_out);
  and u_valC (valC_out, and_3_out, decoder_1_out2);
  Counter #(.width(4), .max('ha), .ongoal("load"), .trigger("falling")) counter_2 (
    .D(4'b0001), .count(and_1_out), .Q(counter_2_q), .clk(clock), .clr(or_5_out));  // open: load, carry
  and and_1 (and_1_out, not_1_out, not_2_out, comparator_2_lt);
  Comparator #(.width(4), .mode("unsigned")) comparator_2 (
    .a(counter_1_q), .b(4'b0100), .lt(comparator_2_lt));  // open: gt, eq
  or or_3 (or_3_out, decoder_1_out4, decoder_1_out0);
  Comparator #(.width(4), .mode("unsigned")) comparator_3 (
    .a(counter_1_q), .b(4'b1011), .eq(comparator_3_eq));  // open: gt, lt
  or rA_rB (rA_rB_out, rA_rB_3_out, rA_rB_2_out);
  or valC_2 (valC_2_out, valC_5_out, valC_3_out);
  and valC_3 (valC_3_out, and_3_out, decoder_1_out1);
  or or_4 (or_4_out, decoder_1_out4, decoder_1_out0);
  Decoder #(.select(3)) decoder_1 (
    .out0(decoder_1_out0), .out1(decoder_1_out1), .out2(decoder_1_out2), .out3(decoder_1_out3),
    .out4(decoder_1_out4), .sel(counter_2_q[2:0]));  // open: out5, out6, out7, en
  not not_1 (not_1_out, and_7_out);
  or or_5 (or_5_out, and_5_out, decoder_2_out0, counter_1_carry);
  Decoder #(.select(4)) decoder_2 (
    .out0(decoder_2_out0), .out1(decoder_2_out1), .out2(decoder_2_out2), .out3(decoder_2_out3),
    .out4(decoder_2_out4), .out5(decoder_2_out5), .out6(decoder_2_out6), .sel(icode));  // open: out7, out8, out9, out10, out11, out12, out13, out14, out15, en
  and valC_4 (valC_4_out, decoder_1_out3, and_4_out);
  and valC_5 (valC_5_out, and_4_out, decoder_1_out2);
  and and_2 (and_2_out, Need_Regids, xor_1_out);
  and rA_rB_2 (rA_rB_2_out, and_2_out, decoder_1_out1);
  and and_3 (and_3_out, xor_1_out, Need_valC);
  not not_2 (not_2_out, and_8_out);
  and rA_rB_3 (rA_rB_3_out, decoder_1_out1, and_4_out);
  and and_4 (and_4_out, Need_Regids, Need_valC);
  and and_5 (and_5_out, decoder_1_out1, nor_1_out);
  Register #(.width(1), .trigger("falling")) register_6 (
    .D(decoder_2_out0), .en(comparator_1_gt), .Q(halt), .clk(clock));  // open: clr
  xor xor_1 (xor_1_out, Need_Regids, Need_valC);
  nor nor_1 (nor_1_out, Need_Regids, Need_valC);
  or or_6 (Need_valC, decoder_2_out2, decoder_2_out3, decoder_2_out4, decoder_2_out6);
  or or_7 (Need_Regids, decoder_2_out1, decoder_2_out2, decoder_2_out3, decoder_2_out4, decoder_2_out5);
  xor xor_2 (xor_2_out, Need_valC, Need_Regids);
  and and_6 (and_6_out, xor_2_out, Need_Regids);
  and and_7 (and_7_out, decoder_1_out2, and_6_out);
  and and_8 (and_8_out, decoder_1_out3, xor_2_out);

  // Notes on the sheet:
  //   contents of rom_1 (hex, n*v repeats v):
  //   20 5f 40 1 20 4f 40 1 20 6f 1 0 40 65 ec ff 20 6f 7 0 40 65 f0 ff 20 6f 4 0 40 65 f4 ff 20 6f 2 0 40
  //   65 f8 ff 20 6f 9 0 40 65 dc ff 20 6f 3 0 40 65 e0 ff 20 6f 6 0 40 65 e4 ff 20 6f 8 0 40 65 e8 ff 20
  //   6f 4 0 40 65 fc ff 20 6f 0 0 40 65 0 0 10 50 20 6f ec ff 50 6 10 53 20 6f dc ff 50 36 10 51 20 6f cc
  //   ff 50 16 10 52 20 6f 0 0 50 26 20 6f 0 0 30 60 0 0 20 7f 0 0 30 73 0 0 50 76 40 71 0 0 20 6f 4 0 50
  //   6 50 36 50 16 20 6f 1 0 20 7f 0 0 30 72 0 0 50 76 40 72 0 0 20 6f ff ff 51 76 30 65 fc ff 50 67 30
  //   72 0 0 61 c0 0 60 78
endmodule

module NEW_PC (
  input  clock,
  input  [15:0] valC,
  input  [15:0] valP,
  input  [3:0] icode,
  input  CC,
  input  [3:0] ifun,
  output [15:0] newPC
);

  wire and_1_out, and_2_out, and_3_out, comparator_1_eq, decoder_1_out6, decoder_2_out0, decoder_2_out1,
       not_1_out, or_1_out;
  wire [3:0] counter_1_q;
  wire [15:0] controlled_buffer_1_out;

  Counter #(.width(4), .max('hb), .ongoal("load")) counter_1 (
    .Q(counter_1_q), .clk(clock));  // open: load, D, count, carry, clr
  Comparator #(.width(4), .mode("unsigned")) comparator_1 (
    .a(counter_1_q), .b(4'b0111), .eq(comparator_1_eq));  // open: gt, lt
  Decoder #(.select(4)) decoder_1 (
    .out6(decoder_1_out6), .sel(icode));  // open: out0, out1, out2, out3, out4, out5, out7, out8, out9, out10, out11, out12, out13, out14, out15, en
  Decoder #(.select(4)) decoder_2 (
    .out0(decoder_2_out0), .out1(decoder_2_out1), .sel(ifun));  // open: out2, out3, out4, out5, out6, out7, out8, out9, out10, out11, out12, out13, out14, out15, en
  and and_1 (and_1_out, decoder_1_out6, decoder_2_out0);
  and and_2 (and_2_out, decoder_1_out6, decoder_2_out1);
  and and_3 (and_3_out, and_2_out, CC);
  or or_1 (or_1_out, and_3_out, and_1_out);
  assign controlled_buffer_1_out = or_1_out ? valC : 16'bz;  // Controlled_Buffer controlled_buffer_1
  Register #(.width(16)) register_1 (.D(controlled_buffer_1_out), .Q(newPC), .clk(comparator_1_eq));  // open: en, clr
  not not_1 (not_1_out, or_1_out);
  assign controlled_buffer_1_out = not_1_out ? valP : 16'bz;  // Controlled_Buffer controlled_buffer_2
endmodule

module PC (
  input  clock,
  input  [15:0] newPC,
  output [15:0] current_PC
);

  wire comparator_1_eq;
  wire [3:0] counter_1_q;

  Counter #(.width(4), .max('hb)) counter_1 (.Q(counter_1_q), .clk(clock));  // open: load, D, count, carry, clr
  Comparator #(.width(4), .mode("unsigned")) comparator_1 (
    .a(counter_1_q), .b(4'b1000), .eq(comparator_1_eq));  // open: gt, lt
  Register #(.width(16)) register_1 (.D(newPC), .Q(current_PC), .clk(comparator_1_eq));  // open: en, clr
endmodule
