// Logisim project memory.circ as structural Verilog: 6 circuits, main circuit main
module main (
  input  [15:0] VAL_E,
  input  [15:0] VAL_A,
  input  [3:0] icode,
  input  clk,
  output [15:0] valM
);

  wire READ_op, WRITE_op;
  wire [15:0] ADDR_op, DATA_op;

  Mem_Read READ (.ICODE(icode), .op(READ_op));
  Mem_Write WRITE (.ICODE(icode), .op(WRITE_op));
  Mem_Addr ADDR (.OP(ADDR_op), .ICODE(icode), .VAL_E(VAL_E));
  DMem DMEM (.clock(clk), .Read(READ_op), .Address(ADDR_op), .Write(WRITE_op), .Data(DATA_op), .valM(valM));
  Mem_Data DATA (.OP(DATA_op), .ICODE(icode), .VAL_A(VAL_A));
endmodule

module DMem (
  input  clock,
  input  Read,
  input  [15:0] Address,
  input  Write,
  input  [15:0] Data,
  output [15:0] valM
);

  wire and_1_out, and_2_out, and_3_out, comparator_1_gt, comparator_2_gt, counter_1_carry, decoder_1_out0,
       decoder_1_out1, decoder_1_out2, decoder_1_out3, not_1_out, not_2_out, xor_1_out;
  wire [3:0] counter_1_q, counter_2_q;
  wire [7:0] controlled_buffer_1_out, controlled_buffer_3_out, controlled_buffer_5_out,
       controlled_buffer_6_out, ram_1_data, register_2_q, register_3_q;
  wire [15:0] adder_1_out, bit_extender_1_out, register_1_q;

  xor xor_1 (xor_1_out, Read, Write);
  and and_1 (and_1_out, xor_1_out, and_2_out);
  Counter #(.width(4), .max('hb)) counter_1 (
    .Q(counter_1_q), .carry(counter_1_carry), .clk(clock));  // open: load, D, count, clr
  Counter #(.width(4), .max('h3)) counter_2 (
    .count(comparator_1_gt), .Q(counter_2_q), .clk(clock), .clr(counter_1_carry));  // open: load, D, carry
  and and_2 (and_2_out, not_1_out, not_2_out, comparator_1_gt);
  Comparator #(.width(4), .mode("unsigned")) comparator_1 (
    .a(counter_1_q), .b(4'b0101), .gt(comparator_1_gt));  // open: eq, lt
  Comparator #(.width(4), .mode("unsigned")) comparator_2 (
    .a(counter_1_q), .b(4'b1000), .gt(comparator_2_gt));  // open: eq, lt
  assign bit_extender_1_out = {{12{1'b0}}, counter_2_q};  // Bit_Extender bit_extender_1
  Decoder #(.select(3)) decoder_1 (
    .out0(decoder_1_out0), .out1(decoder_1_out1), .out2(decoder_1_out2), .out3(decoder_1_out3),
    .sel(counter_2_q[2:0]));  // open: out4, out5, out6, out7, en
  not not_1 (not_1_out, decoder_1_out3);
  not not_2 (not_2_out, decoder_1_out0);
  RAM #(.addrWidth(16)) ram_1 (
    .addr(register_1_q), .data(ram_1_data), .sel(and_1_out), .clk(clock), .ld(Read));  // open: clr
  Adder #(.width(16)) adder_1 (.a(bit_extender_1_out), .b(Address), .out(adder_1_out));  // open: cin, cout
  Register #(.width(16)) register_1 (.D(adder_1_out), .Q(register_1_q), .clk(clock));  // open: en, clr
  assign controlled_buffer_1_out = decoder_1_out1 ? Data[7:0] : 8'bz;  // Controlled_Buffer controlled_buffer_1
  assign controlled_buffer_1_out = decoder_1_out2 ? Data[15:8] : 8'bz;  // Controlled_Buffer controlled_buffer_2
  assign controlled_buffer_3_out = Read ? ram_1_data : 8'bz;  // Controlled_Buffer controlled_buffer_3
  assign ram_1_data = Write ? controlled_buffer_1_out : 8'bz;  // Controlled_Buffer controlled_buffer_4
  assign controlled_buffer_5_out = decoder_1_out1 ? controlled_buffer_3_out : 8'bz;  // Controlled_Buffer controlled_buffer_5
  assign controlled_buffer_6_out = decoder_1_out2 ? controlled_buffer_3_out : 8'bz;  // Controlled_Buffer controlled_buffer_6
  Register register_2 (.D(controlled_buffer_5_out), .Q(register_2_q), .clk(clock));  // open: en, clr
  Register register_3 (.D(controlled_buffer_6_out), .Q(register_3_q), .clk(clock));  // open: en, clr
  Register #(.width(16)) register_4 (
    .D({register_3_q, register_2_q}), .en(and_3_out), .Q(valM), .clk(clock));  // open: clr
  and and_3 (and_3_out, Read, comparator_2_gt);
endmodule

module Mem_Addr (
  input  [15:0] VAL_E,
  input  [3:0] ICODE,
  output [15:0] OP
);

  wire and_1_out, and_2_out, and_3_out, not_1_out, not_2_out, not_3_out, not_4_out, not_5_out, or_1_out;

  not not_1 (not_1_out, ICODE[0]);
  not not_2 (not_2_out, ICODE[1]);
  and and_1 (and_1_out, not_1_out, not_2_out, ICODE[2], not_3_out);
  not not_3 (not_3_out, ICODE[3]);
  and and_2 (and_2_out, ICODE[0], ICODE[1], not_4_out, not_5_out);
  not not_4 (not_4_out, ICODE[2]);
  not not_5 (not_5_out, ICODE[3]);
  or or_1 (or_1_out, and_1_out, and_2_out);
  buf and_3 (and_3_out, or_1_out);  // AND_Gate
  assign OP = and_3_out ? VAL_E : 16'bz;  // Controlled_Buffer controlled_buffer_1
endmodule

module Mem_Data (
  input  [3:0] ICODE,
  input  [15:0] VAL_A,
  output [15:0] OP
);

  wire and_1_out, not_1_out, not_2_out, not_3_out;

  not not_1 (not_1_out, ICODE[0]);
  not not_2 (not_2_out, ICODE[1]);
  not not_3 (not_3_out, ICODE[3]);
  and and_1 (and_1_out, not_1_out, not_2_out, ICODE[2], not_3_out);
  assign OP = and_1_out ? VAL_A : 16'bz;  // Controlled_Buffer controlled_buffer_1
endmodule

module Mem_Read (
  input  [3:0] ICODE,
  output op
);

  wire not_1_out, not_2_out;

  not not_1 (not_1_out, ICODE[2]);
  not not_2 (not_2_out, ICODE[3]);
  and and_1 (op, ICODE[0], ICODE[1], not_1_out, not_2_out);
endmodule

module Mem_Write (
  input  [3:0] ICODE,
  output op
);

  wire not_1_out, not_2_out, not_3_out;

  not not_1 (not_1_out, ICODE[0]);
  not not_2 (not_2_out, ICODE[1]);
  not not_3 (not_3_out, ICODE[3]);
  and and_1 (op, not_1_out, not_2_out, ICODE[2], not_3_out);
endmodule
